# Fritzing sketch IRSensor_bb (saved by Fritzing 0.9.3b)
breadboards: 1

parts:
  Part1 = Arduino Uno (Rev3)
  U1 = TCRT5000 [package=THT]
  R1 = Resistor [tolerance=±5% resistance=220 package=THT]
  R2 = Resistor [tolerance=±5% resistance=220 package=THT]

nets:
  N1: Part1.GND, U1.Pin_1, U1.Pin_2, R1.Pin_1
  N2: Part1.5V, R1.Pin_0, R2.Pin_1
  N3: U1.Pin_3, U1.Pin_4, R2.Pin_0

custom parts:
  TCRT5000: TCRT5000 optical reflective sensor
